# Fritzing sketch Project2 Sketch (saved by Fritzing 0.9.4)
breadboards: 1

parts:
  元件1 = Arduino Uno (Rev3) - ICSP
  J1 = Piezo Speaker
  R1 = Resistor [tolerance=±5% resistance=220 package="1206 [SMD]"]
  kEYPAD_MATRICIAL_1 = KEYPAD 4x3
  LED1 = smd LED [color="Red (633nm)" package="0603 [SMD]"]
  LED2 = smd LED [color="Red (633nm)" package="0603 [SMD]"]
  LED3 = smd LED [color="Red (633nm)" package="0603 [SMD]"]
  LED4 = smd LED [color="Red (633nm)" package="0603 [SMD]"]
  LED5 = smd LED [color="Red (633nm)" package="0603 [SMD]"]
  LED6 = smd LED [color="Red (633nm)" package="0603 [SMD]"]
  LED7 = smd LED [color="Red (633nm)" package="0603 [SMD]"]
  R2 = Resistor [tolerance=±5% resistance=220 package=THT]
  R4 = Resistor [tolerance=±5% resistance=220 package="1206 [SMD]"]
  R5 = Resistor [tolerance=±5% resistance=220 package="1206 [SMD]"]
  R6 = Resistor [tolerance=±5% resistance=220 package="1206 [SMD]"]
  R7 = Resistor [tolerance=±5% resistance=220 package="1206 [SMD]"]
  R8 = Resistor [tolerance=±5% resistance=220 package="1206 [SMD]"]
  R9 = Resistor [tolerance=±5% resistance=220 package="1206 [SMD]"]

nets:
  N1: 元件1.A3, R8.Pin_0
  N2: 元件1.A4/SDA, R9.Pin_0
  N3: 元件1.A5/SCL, R7.Pin_0
  N4: 元件1.ICSP_MISO, 元件1.D12/MISO, R5.Pin_0
  N5: 元件1.D8, kEYPAD_MATRICIAL_1.col1
  N6: 元件1.D9_PWM, R1.Pin_1
  N7: 元件1.D10_PWM/SS, R2.Pin_0
  N8: 元件1.D11_PWM/MOSI, R4.Pin_0
  N9: 元件1.D13/SCK, R6.Pin_0
  N10: 元件1.D2, kEYPAD_MATRICIAL_1.arrow4
  N11: 元件1.D3_PWM, kEYPAD_MATRICIAL_1.arrow3
  N12: 元件1.D4, kEYPAD_MATRICIAL_1.col3
  N13: 元件1.D5_PWM, kEYPAD_MATRICIAL_1.arrow2
  N14: 元件1.D6_PWM, kEYPAD_MATRICIAL_1.col2
  N15: 元件1.D7, kEYPAD_MATRICIAL_1.arrow1
  N16: 元件1.GND, J1.pin1, LED1.cathode, LED2.cathode, LED3.cathode, LED4.cathode, LED5.cathode, LED6.cathode, LED7.cathode
  N17: J1.pin2, R1.Pin_0
  N18: LED1.anode, R2.Pin_1
  N19: LED2.anode, R4.Pin_1
  N20: LED3.anode, R5.Pin_1
  N21: LED4.anode, R6.Pin_1
  N22: LED5.anode, R7.Pin_1
  N23: LED6.anode, R9.Pin_1
  N24: LED7.anode, R8.Pin_1

custom parts:
  KEYPAD 4x3: KEYPAD matricial de 12 botones, 4 filas x 3 columnas
